# Fritzing sketch Sketch (saved by Fritzing 1.0.5)

parts:
  Mod1 = Raspberry Pi Pico W
  OLED_I2C1 = OLED 128x64 I2C Monochrome Display
  M1 = GY-MAX30102

nets:
  N1: Mod1.pin_1, M1.SDA
  N2: Mod1.pin_2, M1.SCL
  GND: Mod1.pin_3, Mod1.pin_38, Mod1.pin_42, OLED_I2C1.GND, M1.GND
  N3: Mod1.pin_31, OLED_I2C1.SDA
  N4: Mod1.pin_32, OLED_I2C1.SCK
  N5: Mod1.pin_36, M1.VIN
  N6: Mod1.pin_40, OLED_I2C1.VDD

custom parts:
  Raspberry Pi Pico W: Raspberry Pi Pico W. Based around the RP2040 microcontroller the Pico W is a low cost microcontroller device bringing Raspberry Pi quality, cost, and easy of use to the microcontroller space. The areas marked KEEPOUT in pcb silkscreen should not have traces running through them to avoid shorts on a soldered in module!
  GY-MAX30102: Oximeter module using the MAX30102 chip. You may wish to read (and check your module) this post on power problems with these modules: https://reedpaper.wordpress.com/2018/08/22/pulse-oximeter-max30100-max30102-how-to-fix-wrong-board/ (may not apply as this is a different module!). As usual, if you want the mounting holes in pcb, you need to drag a hole over the pad in silkscreen to actually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
